// Logisim project cpu.circ as structural Verilog: 6 circuits, main circuit main
module main (
  input  [31:0] INSTRUCTION,
  input  CLOCK,
  output [31:0] PROGRAM_COUNTER,
  output [31:0] ra,
  output [31:0] sp,
  output [31:0] t0,
  output [31:0] t1,
  output [31:0] t2,
  output [31:0] s0,
  output [31:0] s1,
  output [31:0] a0
);

  wire breq, brlt, control_module_1_asel, control_module_1_brun, control_module_1_bsel,
       control_module_1_memrw, control_module_1_pcsel, control_module_1_regwen, DMEM_p1, DMEM_p6, DMEM_p8;
  wire [1:0] control_module_1_load_type, control_module_1_wbsel;
  wire [2:0] control_module_1_immsel;
  wire [3:0] control_module_1_alusel;
  wire [31:0] aluPC, DMEM_p10, immediate_generator_1_immout, lb_lh_splitter_1_lb_val,
       lb_lh_splitter_1_lh_val, multiplexer_1_out, multiplexer_2_out, multiplexer_3_out, multiplexer_4_out,
       multiplexer_5_out, multiplexer_6_out, pc_plus_4, RegFile_read_data_1, RegFile_read_data_2,
       register_1_q, subtractor_1_out;

  Adder #(.width(32)) adder_1 (.a(PROGRAM_COUNTER), .b(32'h4), .out(pc_plus_4));  // open: cin, cout
  Multiplexer #(.width(32), .enable("false")) multiplexer_1 (
    .in0(pc_plus_4), .in1(aluPC), .out(multiplexer_1_out), .sel(control_module_1_pcsel));
  Register #(.width(32)) PC (.D(multiplexer_1_out), .en(1'b1), .clk(CLOCK), .Q(PROGRAM_COUNTER));  // open: clr
  Multiplexer #(.width(32), .enable("false")) multiplexer_2 (
    .in0(INSTRUCTION), .in1(32'h13), .out(multiplexer_2_out), .sel(control_module_1_pcsel));
  Register #(.width(32)) register_1 (.D(multiplexer_2_out), .en(1'b1), .clk(CLOCK), .Q(register_1_q));  // open: clr
  control_module control_module_1 (
    .Instruction_32(register_1_q), .BrEq(breq), .BrLt(brlt), .ALUSel(control_module_1_alusel),
    .ASel(control_module_1_asel), .BSel(control_module_1_bsel), .MemRW(control_module_1_memrw),
    .BrUn(control_module_1_brun), .RegWEn(control_module_1_regwen), .PCSel(control_module_1_pcsel),
    .WBSel(control_module_1_wbsel), .load_type(control_module_1_load_type), .ImmSel(control_module_1_immsel));
  Subtractor #(.width(32)) subtractor_1 (.a(PROGRAM_COUNTER), .b(32'h4), .out(subtractor_1_out));  // open: bin, bout
  immediate_generator immediate_generator_1 (
    .ImmSel(control_module_1_immsel), .imm(register_1_q[31:7]), .immOut(immediate_generator_1_immout));
  regfile_main RegFile (
    .rs2(register_1_q[24:20]), .rd(register_1_q[11:7]), .Read_Data_1(RegFile_read_data_1),
    .Read_Data_2(RegFile_read_data_2), .ra(ra), .sp(sp), .t0(t0), .t1(t1), .t2(t2), .s0(s0), .s1(s1),
    .a0(a0), .rs1(register_1_q[19:15]), .Write_Data(multiplexer_6_out), .RegWEn(control_module_1_regwen),
    .clk(CLOCK));
  branch_comp branch_comp_1 (
    .rs1(RegFile_read_data_1), .rs2(RegFile_read_data_2), .BrUn(control_module_1_brun), .BrEq(breq),
    .BrLT(brlt));
  Multiplexer #(.width(32), .enable("false")) multiplexer_3 (
    .in0(RegFile_read_data_2), .in1(immediate_generator_1_immout), .out(multiplexer_3_out),
    .sel(control_module_1_bsel));
  Multiplexer #(.width(32), .enable("false")) multiplexer_4 (
    .in0(RegFile_read_data_1), .in1(subtractor_1_out), .out(multiplexer_4_out), .sel(control_module_1_asel));
  alu Arithmetic_Logic_Unit (
    .B(multiplexer_3_out), .Result(aluPC), .A(multiplexer_4_out), .ALUSel(control_module_1_alusel));
  // mem_main DMEM: pin names not known; wires that end beside it: DMEM_p1, aluPC, RegFile_read_data_2, DMEM_p1, CLOCK, DMEM_p6, DMEM_p6, DMEM_p8, control_module_1_memrw, DMEM_p10
  lb_lh_splitter lb_lh_splitter_1 (
    .val_at_address(DMEM_p10), .unfiltered_imm(register_1_q[31:7]), .address_to_access(aluPC),
    .lb_val(lb_lh_splitter_1_lb_val), .lh_val(lb_lh_splitter_1_lh_val));
  Multiplexer #(.select(2), .width(32), .enable("false")) multiplexer_5 (
    .in0(DMEM_p10), .in1(lb_lh_splitter_1_lb_val), .in2(lb_lh_splitter_1_lh_val), .out(multiplexer_5_out),
    .sel(control_module_1_load_type));  // open: in3
  Multiplexer #(.select(2), .width(32), .enable("false")) multiplexer_6 (
    .in0(PROGRAM_COUNTER), .in1(aluPC), .in2(multiplexer_5_out), .out(multiplexer_6_out),
    .sel(control_module_1_wbsel));  // open: in3

  // Other names for the same wires on the sheet: clk = CLOCK

  // Notes on the sheet:
  //   Output
  //   IMEM (do **NOT** move this)
  //   Inputs
  //   Inputs/Outputs for testing. Do **NOT** move these.
endmodule

module control_module (
  input  [31:0] Instruction_32,
  input  BrEq,
  input  BrLt,
  output [3:0] ALUSel,
  output ASel,
  output BSel,
  output MemRW,
  output BrUn,
  output RegWEn,
  output PCSel,
  output [1:0] WBSel,
  output [1:0] load_type,
  output [2:0] ImmSel
);

  wire add, and_2_out, and_3_out, and_4_out, and_5_out, and_6_out, and_7_out, and_8_out, and_11_out,
       and_12_out, and_13_out, and_14_out, and_15_out, and_16_out, and_17_out, and_18_out, and_19_out,
       and_20_out, and_21_out, and_22_out, and_23_out, and_24_out, and_25_out, and_26_out, and_27_out,
       and_28_out, and_29_out, and_30_out, and_31_out, and_32_out, and_33_out, and_34_out, and_35_out,
       and_36_out, and_37_out, and_38_out, and_39_out, and_40_out, and_41_out, and_42_out, and_43_out,
       and_44_out, and_45_out, and_46_out, comparator_1_eq, comparator_2_eq, comparator_3_eq,
       comparator_4_eq, comparator_5_eq, comparator_9_eq, comparator_10_eq, comparator_11_eq,
       comparator_12_eq, comparator_13_eq, comparator_14_eq, comparator_15_eq, comparator_16_eq,
       comparator_17_eq, comparator_18_eq, comparator_19_eq, comparator_20_eq, comparator_21_eq,
       comparator_22_eq, comparator_23_eq, comparator_24_eq, comparator_25_eq, comparator_26_eq,
       comparator_27_eq, comparator_28_eq, comparator_29_eq, comparator_30_eq, comparator_31_eq,
       comparator_32_eq, comparator_33_eq, comparator_34_eq, comparator_35_eq, comparator_36_eq,
       comparator_37_eq, comparator_38_eq, comparator_39_eq, comparator_40_eq, comparator_41_eq,
       comparator_42_eq, comparator_43_eq, comparator_44_eq, comparator_45_eq, comparator_46_eq,
       comparator_47_eq, comparator_48_eq, comparator_49_eq, comparator_50_eq, comparator_51_eq,
       comparator_52_eq, comparator_53_eq, comparator_54_eq, comparator_55_eq, comparator_56_eq,
       comparator_57_eq, comparator_58_eq, comparator_59_eq, comparator_60_eq, comparator_61_eq,
       comparator_62_eq, comparator_63_eq, comparator_64_eq, comparator_65_eq, comparator_66_eq,
       comparator_67_eq, comparator_68_eq, comparator_69_eq, comparator_70_eq, comparator_71_eq,
       comparator_72_eq, comparator_73_eq, comparator_74_eq, comparator_75_eq, comparator_76_eq,
       comparator_77_eq, comparator_78_eq, comparator_79_eq, comparator_80_eq, comparator_81_eq,
       comparator_82_eq, comparator_83_eq, comparator_84_eq, comparator_85_eq, comparator_86_eq,
       comparator_87_eq, comparator_88_eq, comparator_89_eq, comparator_90_eq, comparator_91_eq,
       comparator_92_eq, comparator_93_eq, comparator_94_eq, comparator_95_eq, comparator_96_eq,
       comparator_97_eq, comparator_98_eq, comparator_99_eq, comparator_100_eq, isAdd, isMul, isSub,
       not_1_out, not_2_out, not_3_out, not_4_out, not_5_out, not_6_out, not_7_out, not_8_out, not_9_out,
       not_10_out, not_11_out, not_12_out, not_13_out, not_14_out, not_16_out, or_1_out, or_5_out, or_6_out,
       or_7_out, or_8_out, or_9_out, or_10_out, or_11_out, or_12_out, or_13_out;
  wire [1:0] multiplexer_2_out, multiplexer_3_out, multiplexer_4_out, multiplexer_6_out, multiplexer_10_out,
       multiplexer_11_out, multiplexer_12_out;
  wire [2:0] multiplexer_9_out;
  wire [3:0] multiplexer_13_out, multiplexer_14_out, multiplexer_15_out, multiplexer_16_out,
       multiplexer_17_out, multiplexer_18_out, multiplexer_19_out, multiplexer_20_out, multiplexer_21_out,
       multiplexer_22_out, multiplexer_23_out, multiplexer_24_out, multiplexer_25_out, undriven_2;
  wire [16:0] instID;
  wire [31:0] undriven;

  not not_1 (not_1_out, undriven[31]);
  not not_2 (not_2_out, undriven[30]);
  not not_3 (not_3_out, undriven[29]);
  not not_4 (not_4_out, undriven[28]);
  not not_5 (not_5_out, undriven[27]);
  not not_6 (not_6_out, undriven[26]);
  not not_7 (not_7_out, undriven[25]);
  not not_8 (not_8_out, undriven[14]);
  not not_9 (not_9_out, undriven[13]);
  and and_1 (add, not_1_out, not_2_out, not_3_out, not_4_out, not_5_out, not_6_out, not_7_out, not_8_out, not_9_out, not_10_out, not_11_out, undriven[5], undriven[4], not_12_out, not_13_out, undriven[1], undriven[0]);
  not not_10 (not_10_out, undriven[12]);
  not not_11 (not_11_out, undriven[6]);
  not not_12 (not_12_out, undriven[3]);
  not not_13 (not_13_out, undriven[2]);
  Comparator #(.width(3), .mode("unsigned")) comparator_1 (
    .a(ImmSel), .b(3'b100), .eq(comparator_1_eq));  // open: gt, lt
  Comparator #(.width(3), .mode("unsigned")) comparator_2 (
    .a(Instruction_32[14:12]), .b(3'b000), .eq(comparator_2_eq));  // open: gt, lt
  Comparator #(.width(3), .mode("unsigned")) comparator_3 (
    .a(Instruction_32[14:12]), .b(3'b001), .eq(comparator_3_eq));  // open: gt, lt
  Comparator #(.width(3), .mode("unsigned")) comparator_4 (
    .a(Instruction_32[14:12]), .b(3'b100), .eq(comparator_4_eq));  // open: gt, lt
  Comparator #(.width(3), .mode("unsigned")) comparator_5 (
    .a(Instruction_32[14:12]), .b(3'b110), .eq(comparator_5_eq));  // open: gt, lt
  Multiplexer #(.width(4), .enable("false")) multiplexer_1 (.in0(undriven_2), .in1(4'b1101));  // open: out, sel
  Comparator #(.width(17), .mode("unsigned")) comparator_6 (.a(instID), .b({17{1'b0}}), .eq(isAdd));  // open: gt, lt
  Comparator #(.width(17), .mode("unsigned")) comparator_7 (.a(instID), .b({17{1'b0}}), .eq(isMul));  // open: gt, lt
  Comparator #(.width(17), .mode("unsigned")) comparator_8 (.a(instID), .b({17{1'b0}}), .eq(isSub));  // open: gt, lt
  Comparator #(.width(7), .mode("unsigned")) comparator_9 (
    .a(Instruction_32[6:0]), .b(7'b1100111), .eq(comparator_9_eq));  // open: gt, lt
  not not_14 (not_14_out, BrEq);
  Comparator #(.width(3), .mode("unsigned")) comparator_10 (
    .a(ImmSel), .b(3'b011), .eq(comparator_10_eq));  // open: gt, lt
  Comparator #(.width(3), .mode("unsigned")) comparator_11 (
    .a(Instruction_32[14:12]), .b(3'b010), .eq(comparator_11_eq));  // open: gt, lt
  Comparator #(.width(3), .mode("unsigned")) comparator_12 (
    .a(ImmSel), .b(3'b100), .eq(comparator_12_eq));  // open: gt, lt
  Comparator #(.width(3), .mode("unsigned")) comparator_13 (
    .a(Instruction_32[14:12]), .b(3'b110), .eq(comparator_13_eq));  // open: gt, lt
  Comparator #(.width(3), .mode("unsigned")) comparator_14 (
    .a(ImmSel), .b(3'b001), .eq(comparator_14_eq));  // open: gt, lt
  Comparator #(.width(3), .mode("unsigned")) comparator_15 (
    .a(ImmSel), .b(3'b010), .eq(comparator_15_eq));  // open: gt, lt
  Comparator #(.width(3), .mode("unsigned")) comparator_16 (
    .a(ImmSel), .b(3'b101), .eq(comparator_16_eq));  // open: gt, lt
  Comparator #(.width(3), .mode("unsigned")) comparator_17 (
    .a(ImmSel), .b(3'b110), .eq(comparator_17_eq));  // open: gt, lt
  Comparator #(.width(3), .mode("unsigned")) comparator_18 (
    .a(ImmSel), .b(3'b110), .eq(comparator_18_eq));  // open: gt, lt
  and and_2 (and_2_out, comparator_1_eq, BrEq, comparator_2_eq);
  and and_3 (and_3_out, comparator_1_eq, not_14_out, comparator_3_eq);
  and and_4 (and_4_out, comparator_1_eq, BrLt, comparator_4_eq);
  and and_5 (and_5_out, comparator_1_eq, BrLt, comparator_5_eq);
  Comparator #(.width(3), .mode("unsigned")) comparator_19 (
    .a(ImmSel), .b(3'b110), .eq(comparator_19_eq));  // open: gt, lt
  Comparator #(.width(7), .mode("unsigned")) comparator_20 (
    .a(Instruction_32[6:0]), .b(7'b1100111), .eq(comparator_20_eq));  // open: gt, lt
  Comparator #(.width(7), .mode("unsigned")) comparator_21 (
    .a(Instruction_32[6:0]), .b(7'b0000011), .eq(comparator_21_eq));  // open: gt, lt
  Comparator #(.width(3), .mode("unsigned")) comparator_22 (
    .a(Instruction_32[14:12]), .b(3'b010), .eq(comparator_22_eq));  // open: gt, lt
  Comparator #(.width(7), .mode("unsigned")) comparator_23 (
    .a(Instruction_32[6:0]), .b(7'b0000011), .eq(comparator_23_eq));  // open: gt, lt
  Comparator #(.width(3), .mode("unsigned")) comparator_24 (
    .a(Instruction_32[14:12]), .b(3'b000), .eq(comparator_24_eq));  // open: gt, lt
  Comparator #(.width(7), .mode("unsigned")) comparator_25 (
    .a(Instruction_32[6:0]), .b(7'b0000011), .eq(comparator_25_eq));  // open: gt, lt
  and and_6 (and_6_out, comparator_25_eq, comparator_26_eq);
  Comparator #(.width(3), .mode("unsigned")) comparator_26 (
    .a(Instruction_32[14:12]), .b(3'b001), .eq(comparator_26_eq));  // open: gt, lt
  Comparator #(.width(3), .mode("unsigned")) comparator_27 (
    .a(ImmSel), .b(3'b100), .eq(comparator_27_eq));  // open: gt, lt
  Comparator #(.width(3), .mode("unsigned")) comparator_28 (
    .a(ImmSel), .b(3'b110), .eq(comparator_28_eq));  // open: gt, lt
  or or_1 (or_1_out, comparator_19_eq, comparator_20_eq);
  and and_7 (and_7_out, comparator_21_eq, comparator_22_eq);
  and and_8 (and_8_out, comparator_23_eq, comparator_24_eq);
  Comparator #(.width(3), .mode("unsigned")) comparator_29 (
    .a(ImmSel), .b(3'b001), .eq(comparator_29_eq));  // open: gt, lt
  and and_9 (MemRW, comparator_10_eq, comparator_11_eq);
  and and_10 (BrUn, comparator_12_eq, comparator_13_eq);
  or or_2 (RegWEn, comparator_14_eq, comparator_15_eq, comparator_16_eq, comparator_17_eq);
  or or_3 (PCSel, comparator_18_eq, comparator_9_eq, and_2_out, and_3_out, and_4_out, and_5_out);
  Multiplexer #(.width(2), .enable("false")) multiplexer_2 (
    .in0(2'b01), .in1(2'b00), .out(multiplexer_2_out), .sel(or_1_out));
  Comparator #(.width(3), .mode("unsigned")) comparator_30 (
    .a(ImmSel), .b(3'b010), .eq(comparator_30_eq));  // open: gt, lt
  Comparator #(.width(3), .mode("unsigned")) comparator_31 (
    .a(Instruction_32[14:12]), .b(3'b010), .eq(comparator_31_eq));  // open: gt, lt
  or or_4 (ASel, comparator_27_eq, comparator_28_eq);
  not not_15 (BSel, comparator_29_eq);
  Multiplexer #(.width(2), .enable("false")) multiplexer_3 (
    .in0(multiplexer_2_out), .in1(2'b10), .out(multiplexer_3_out), .sel(or_5_out));
  or or_5 (or_5_out, and_7_out, and_8_out, and_6_out);
  Multiplexer #(.width(2), .enable("false")) multiplexer_4 (
    .in0(2'b00), .in1(2'b00), .out(multiplexer_4_out), .sel(and_11_out));
  and and_11 (and_11_out, comparator_30_eq, comparator_31_eq);
  Comparator #(.width(3), .mode("unsigned")) comparator_32 (
    .a(ImmSel), .b(3'b010), .eq(comparator_32_eq));  // open: gt, lt
  Comparator #(.width(3), .mode("unsigned")) comparator_33 (
    .a(Instruction_32[14:12]), .b(3'b000), .eq(comparator_33_eq));  // open: gt, lt
  Comparator #(.width(7), .mode("unsigned")) comparator_34 (
    .a(Instruction_32[6:0]), .b(7'b0000011), .eq(comparator_34_eq));  // open: gt, lt
  Comparator #(.width(3), .mode("unsigned")) comparator_35 (
    .a(Instruction_32[14:12]), .b(3'b000), .eq(comparator_35_eq));  // open: gt, lt
  Comparator #(.width(3), .mode("unsigned")) comparator_36 (
    .a(ImmSel), .b(3'b100), .eq(comparator_36_eq));  // open: gt, lt
  Comparator #(.width(3), .mode("unsigned")) comparator_37 (
    .a(Instruction_32[14:12]), .b(3'b000), .eq(comparator_37_eq));  // open: gt, lt
  Comparator #(.width(3), .mode("unsigned")) comparator_38 (
    .a(Instruction_32[14:12]), .b(3'b001), .eq(comparator_38_eq));  // open: gt, lt
  Comparator #(.width(3), .mode("unsigned")) comparator_39 (
    .a(Instruction_32[14:12]), .b(3'b100), .eq(comparator_39_eq));  // open: gt, lt
  Comparator #(.width(3), .mode("unsigned")) comparator_40 (
    .a(Instruction_32[14:12]), .b(3'b110), .eq(comparator_40_eq));  // open: gt, lt
  type_determiner type_determiner_1 (.Opcode(Instruction_32[6:0]), .InstrType(ImmSel));
  Multiplexer #(.width(2), .enable("false")) multiplexer_5 (
    .in0(multiplexer_3_out), .in1(2'b01), .out(WBSel), .sel(1'b0));
  Multiplexer #(.width(2), .enable("false")) multiplexer_6 (
    .in0(multiplexer_4_out), .in1(2'b01), .out(multiplexer_6_out), .sel(and_12_out));
  and and_12 (and_12_out, comparator_32_eq, comparator_33_eq);
  Comparator #(.width(3), .mode("unsigned")) comparator_41 (
    .a(ImmSel), .b(3'b010), .eq(comparator_41_eq));  // open: gt, lt
  Comparator #(.width(3), .mode("unsigned")) comparator_42 (
    .a(Instruction_32[14:12]), .b(3'b001), .eq(comparator_42_eq));  // open: gt, lt
  and and_13 (and_13_out, comparator_34_eq, comparator_35_eq);
  Comparator #(.width(7), .mode("unsigned")) comparator_43 (
    .a(Instruction_32[6:0]), .b(7'b0000011), .eq(comparator_43_eq));  // open: gt, lt
  Comparator #(.width(3), .mode("unsigned")) comparator_44 (
    .a(Instruction_32[14:12]), .b(3'b001), .eq(comparator_44_eq));  // open: gt, lt
  Multiplexer #(.width(2), .enable("false")) multiplexer_7 (
    .in0(multiplexer_6_out), .in1(2'b10), .out(load_type), .sel(and_14_out));
  and and_14 (and_14_out, comparator_41_eq, comparator_42_eq);
  Multiplexer #(.width(3), .enable("false")) multiplexer_8 (
    .in0(multiplexer_9_out), .in1(3'b111), .sel(and_15_out));  // open: out
  Multiplexer #(.width(3), .enable("false")) multiplexer_9 (
    .in1(3'b000), .out(multiplexer_9_out), .sel(and_13_out));  // open: in0
  and and_15 (and_15_out, comparator_43_eq, comparator_44_eq);
  Multiplexer #(.width(2), .enable("false")) multiplexer_10 (
    .in0(2'b00), .in1(2'b11), .out(multiplexer_10_out), .sel(and_17_out));
  and and_16 (and_16_out, comparator_36_eq, BrEq, comparator_37_eq);
  and and_17 (and_17_out, comparator_36_eq, not_16_out, comparator_38_eq);
  not not_16 (not_16_out, BrEq);
  and and_18 (and_18_out, comparator_36_eq, BrLt, comparator_39_eq);
  and and_19 (and_19_out, comparator_36_eq, BrLt, comparator_40_eq);
  Multiplexer #(.width(2), .enable("false")) multiplexer_11 (
    .in0(multiplexer_10_out), .in1(2'b10), .out(multiplexer_11_out), .sel(or_6_out));
  or or_6 (or_6_out, and_18_out, and_19_out);
  Comparator #(.width(7), .mode("unsigned")) comparator_45 (
    .a(Instruction_32[6:0]), .b(7'b0010011), .eq(comparator_45_eq));  // open: gt, lt
  Comparator #(.width(3), .mode("unsigned")) comparator_46 (
    .a(Instruction_32[14:12]), .b(3'b001), .eq(comparator_46_eq));  // open: gt, lt
  Comparator #(.width(7), .mode("unsigned")) comparator_47 (
    .a(Instruction_32[31:25]), .b({7{1'b0}}), .eq(comparator_47_eq));  // open: gt, lt
  Multiplexer #(.width(2), .enable("false")) multiplexer_12 (
    .in0(multiplexer_11_out), .in1(2'b01), .out(multiplexer_12_out), .sel(and_16_out));
  Comparator #(.width(3), .mode("unsigned")) comparator_48 (
    .a(ImmSel), .b(3'b001), .eq(comparator_48_eq));  // open: gt, lt
  Comparator #(.width(10), .mode("unsigned")) comparator_49 (
    .a({Instruction_32[31:25], Instruction_32[14:12]}), .b(10'h2), .eq(comparator_49_eq));  // open: gt, lt
  Comparator #(.width(3), .mode("unsigned")) comparator_50 (
    .a(ImmSel), .b(3'b001), .eq(comparator_50_eq));  // open: gt, lt
  and and_20 (and_20_out, comparator_50_eq, comparator_51_eq);
  Comparator #(.width(10), .mode("unsigned")) comparator_51 (
    .a({Instruction_32[31:25], Instruction_32[14:12]}), .b(10'h9), .eq(comparator_51_eq));  // open: gt, lt
  and and_21 (and_21_out, comparator_48_eq, comparator_49_eq);
  Comparator #(.width(7), .mode("unsigned")) comparator_52 (
    .a(Instruction_32[6:0]), .b(7'b0010011), .eq(comparator_52_eq));  // open: gt, lt
  Comparator #(.width(3), .mode("unsigned")) comparator_53 (
    .a(Instruction_32[14:12]), .b(3'b010), .eq(comparator_53_eq));  // open: gt, lt
  and and_22 (and_22_out, comparator_45_eq, comparator_46_eq, comparator_47_eq);
  Comparator #(.width(3), .mode("unsigned")) comparator_54 (
    .a(ImmSel), .b(3'b010), .eq(comparator_54_eq));  // open: gt, lt
  Comparator #(.width(3), .mode("unsigned")) comparator_55 (
    .a(Instruction_32[14:12]), .b(3'b101), .eq(comparator_55_eq));  // open: gt, lt
  Comparator #(.width(7), .mode("unsigned")) comparator_56 (
    .a(Instruction_32[31:25]), .b({7{1'b0}}), .eq(comparator_56_eq));  // open: gt, lt
  Comparator #(.width(3), .mode("unsigned")) comparator_57 (
    .a(ImmSel), .b(3'b001), .eq(comparator_57_eq));  // open: gt, lt
  and and_23 (and_23_out, comparator_57_eq, comparator_58_eq);
  Comparator #(.width(10), .mode("unsigned")) comparator_58 (
    .a({Instruction_32[31:25], Instruction_32[14:12]}), .b({10{1'b0}}), .eq(comparator_58_eq));  // open: gt, lt
  Comparator #(.width(7), .mode("unsigned")) comparator_59 (
    .a(Instruction_32[6:0]), .b(7'b0010011), .eq(comparator_59_eq));  // open: gt, lt
  Multiplexer #(.width(4), .enable("false")) multiplexer_13 (
    .in0(4'b0000), .in1(4'b1110), .out(multiplexer_13_out), .sel(and_20_out));
  Comparator #(.width(3), .mode("unsigned")) comparator_60 (
    .a(ImmSel), .b(3'b001), .eq(comparator_60_eq));  // open: gt, lt
  and and_24 (and_24_out, comparator_60_eq, comparator_61_eq);
  Comparator #(.width(10), .mode("unsigned")) comparator_61 (
    .a({Instruction_32[31:25], Instruction_32[14:12]}), .b(10'h100), .eq(comparator_61_eq));  // open: gt, lt
  and and_25 (and_25_out, comparator_52_eq, comparator_53_eq);
  and and_26 (and_26_out, comparator_54_eq, comparator_55_eq, comparator_56_eq);
  Multiplexer #(.width(4), .enable("false")) multiplexer_14 (
    .in0(multiplexer_13_out), .in1(4'b1100), .out(multiplexer_14_out), .sel(and_24_out));
  Comparator #(.width(3), .mode("unsigned")) comparator_62 (
    .a(ImmSel), .b(3'b001), .eq(comparator_62_eq));  // open: gt, lt
  and and_27 (and_27_out, comparator_62_eq, comparator_63_eq);
  Comparator #(.width(10), .mode("unsigned")) comparator_63 (
    .a({Instruction_32[31:25], Instruction_32[14:12]}), .b(10'hb), .eq(comparator_63_eq));  // open: gt, lt
  Comparator #(.width(3), .mode("unsigned")) comparator_64 (
    .a(ImmSel), .b(3'b010), .eq(comparator_64_eq));  // open: gt, lt
  Comparator #(.width(3), .mode("unsigned")) comparator_65 (
    .a(Instruction_32[14:12]), .b(3'b101), .eq(comparator_65_eq));  // open: gt, lt
  Comparator #(.width(7), .mode("unsigned")) comparator_66 (
    .a(Instruction_32[31:25]), .b(7'b0100000), .eq(comparator_66_eq));  // open: gt, lt
  Multiplexer #(.width(4), .enable("false")) multiplexer_15 (
    .in0(multiplexer_14_out), .in1(4'b1011), .out(multiplexer_15_out), .sel(and_27_out));
  Comparator #(.width(3), .mode("unsigned")) comparator_67 (
    .a(ImmSel), .b(3'b001), .eq(comparator_67_eq));  // open: gt, lt
  and and_28 (and_28_out, comparator_67_eq, comparator_68_eq);
  Comparator #(.width(10), .mode("unsigned")) comparator_68 (
    .a({Instruction_32[31:25], Instruction_32[14:12]}), .b(10'h8), .eq(comparator_68_eq));  // open: gt, lt
  Comparator #(.width(3), .mode("unsigned")) comparator_69 (
    .a(ImmSel), .b(3'b001), .eq(comparator_69_eq));  // open: gt, lt
  Comparator #(.width(10), .mode("unsigned")) comparator_70 (
    .a({Instruction_32[31:25], Instruction_32[14:12]}), .b(10'h4), .eq(comparator_70_eq));  // open: gt, lt
  Comparator #(.width(7), .mode("unsigned")) comparator_71 (
    .a(Instruction_32[6:0]), .b(7'b0000011), .eq(comparator_71_eq));  // open: gt, lt
  and and_29 (and_29_out, comparator_71_eq, comparator_72_eq);
  Comparator #(.width(3), .mode("unsigned")) comparator_72 (
    .a(Instruction_32[14:12]), .b(3'b010), .eq(comparator_72_eq));  // open: gt, lt
  Comparator #(.width(3), .mode("unsigned")) comparator_73 (
    .a(Instruction_32[14:12]), .b(3'b000), .eq(comparator_73_eq));  // open: gt, lt
  Multiplexer #(.width(4), .enable("false")) multiplexer_16 (
    .in0(multiplexer_15_out), .in1(4'b1010), .out(multiplexer_16_out), .sel(and_28_out));
  Comparator #(.width(3), .mode("unsigned")) comparator_74 (
    .a(ImmSel), .b(3'b001), .eq(comparator_74_eq));  // open: gt, lt
  and and_30 (and_30_out, comparator_74_eq, comparator_75_eq);
  Comparator #(.width(10), .mode("unsigned")) comparator_75 (
    .a({Instruction_32[31:25], Instruction_32[14:12]}), .b(10'hf), .eq(comparator_75_eq));  // open: gt, lt
  Comparator #(.width(3), .mode("unsigned")) comparator_76 (
    .a(ImmSel), .b(3'b001), .eq(comparator_76_eq));  // open: gt, lt
  Comparator #(.width(10), .mode("unsigned")) comparator_77 (
    .a({Instruction_32[31:25], Instruction_32[14:12]}), .b(10'h5), .eq(comparator_77_eq));  // open: gt, lt
  and and_31 (and_31_out, comparator_69_eq, comparator_70_eq);
  and and_32 (and_32_out, comparator_71_eq, comparator_59_eq, comparator_73_eq);
  Comparator #(.width(3), .mode("unsigned")) comparator_78 (
    .a(ImmSel), .b(3'b011), .eq(comparator_78_eq));  // open: gt, lt
  Comparator #(.width(3), .mode("unsigned")) comparator_79 (
    .a(Instruction_32[14:12]), .b(3'b010), .eq(comparator_79_eq));  // open: gt, lt
  Multiplexer #(.width(4), .enable("false")) multiplexer_17 (
    .in0(multiplexer_16_out), .in1(4'b1001), .out(multiplexer_17_out), .sel(and_30_out));
  Comparator #(.width(3), .mode("unsigned")) comparator_80 (
    .a(ImmSel), .b(3'b001), .eq(comparator_80_eq));  // open: gt, lt
  and and_33 (and_33_out, comparator_80_eq, comparator_81_eq);
  Comparator #(.width(10), .mode("unsigned")) comparator_81 (
    .a({Instruction_32[31:25], Instruction_32[14:12]}), .b(10'hd), .eq(comparator_81_eq));  // open: gt, lt
  Comparator #(.width(3), .mode("unsigned")) comparator_82 (
    .a(ImmSel), .b(3'b001), .eq(comparator_82_eq));  // open: gt, lt
  Comparator #(.width(10), .mode("unsigned")) comparator_83 (
    .a({Instruction_32[31:25], Instruction_32[14:12]}), .b(10'h1), .eq(comparator_83_eq));  // open: gt, lt
  and and_34 (and_34_out, comparator_76_eq, comparator_77_eq);
  Comparator #(.width(3), .mode("unsigned")) comparator_84 (
    .a(ImmSel), .b(3'b001), .eq(comparator_84_eq));  // open: gt, lt
  and and_35 (and_35_out, comparator_84_eq, comparator_85_eq);
  Comparator #(.width(10), .mode("unsigned")) comparator_85 (
    .a({Instruction_32[31:25], Instruction_32[14:12]}), .b(10'h6), .eq(comparator_85_eq));  // open: gt, lt
  and and_36 (and_36_out, comparator_78_eq, comparator_79_eq);
  Comparator #(.width(3), .mode("unsigned")) comparator_86 (
    .a(ImmSel), .b(3'b100), .eq(comparator_86_eq));  // open: gt, lt
  Comparator #(.width(3), .mode("unsigned")) comparator_87 (
    .a(Instruction_32[14:12]), .b(3'b000), .eq(comparator_87_eq));  // open: gt, lt
  Comparator #(.width(3), .mode("unsigned")) comparator_88 (
    .a(Instruction_32[14:12]), .b(3'b100), .eq(comparator_88_eq));  // open: gt, lt
  Multiplexer #(.width(4), .enable("false")) multiplexer_18 (
    .in0(multiplexer_17_out), .in1(4'b1000), .out(multiplexer_18_out), .sel(and_33_out));
  or or_7 (or_7_out, and_21_out, and_25_out);
  and and_37 (and_37_out, comparator_82_eq, comparator_83_eq);
  Comparator #(.width(3), .mode("unsigned")) comparator_89 (
    .a(ImmSel), .b(3'b001), .eq(comparator_89_eq));  // open: gt, lt
  Comparator #(.width(10), .mode("unsigned")) comparator_90 (
    .a({Instruction_32[31:25], Instruction_32[14:12]}), .b(10'h7), .eq(comparator_90_eq));  // open: gt, lt
  and and_38 (and_38_out, comparator_86_eq, comparator_87_eq);
  and and_39 (and_39_out, comparator_86_eq, comparator_88_eq);
  and and_40 (and_40_out, comparator_86_eq, comparator_91_eq);
  Comparator #(.width(3), .mode("unsigned")) comparator_91 (
    .a(Instruction_32[14:12]), .b(3'b110), .eq(comparator_91_eq));  // open: gt, lt
  Comparator #(.width(3), .mode("unsigned")) comparator_92 (
    .a(Instruction_32[14:12]), .b(3'b001), .eq(comparator_92_eq));  // open: gt, lt
  Multiplexer #(.width(4), .enable("false")) multiplexer_19 (
    .in0(multiplexer_18_out), .in1(4'b0111), .out(multiplexer_19_out), .sel(or_7_out));
  or or_8 (or_8_out, and_37_out, and_22_out);
  and and_41 (and_41_out, comparator_89_eq, comparator_90_eq);
  and and_42 (and_42_out, comparator_86_eq, comparator_92_eq);
  Comparator #(.width(3), .mode("unsigned")) comparator_93 (
    .a(ImmSel), .b(3'b110), .eq(comparator_93_eq));  // open: gt, lt
  Comparator #(.width(7), .mode("unsigned")) comparator_94 (
    .a(Instruction_32[6:0]), .b(7'b1100111), .eq(comparator_94_eq));  // open: gt, lt
  Multiplexer #(.width(4), .enable("false")) multiplexer_20 (
    .in0(multiplexer_19_out), .in1(4'b0110), .out(multiplexer_20_out), .sel(or_8_out));
  and and_43 (and_43_out, comparator_64_eq, comparator_65_eq, comparator_66_eq);
  Comparator #(.width(3), .mode("unsigned")) comparator_95 (
    .a(ImmSel), .b(3'b010), .eq(comparator_95_eq));  // open: gt, lt
  Comparator #(.width(3), .mode("unsigned")) comparator_96 (
    .a(Instruction_32[14:12]), .b(3'b100), .eq(comparator_96_eq));  // open: gt, lt
  Multiplexer #(.width(4), .enable("false")) multiplexer_21 (
    .in0(multiplexer_20_out), .in1(4'b0101), .out(multiplexer_21_out), .sel(and_43_out));
  and and_44 (and_44_out, comparator_95_eq, comparator_96_eq);
  Comparator #(.width(3), .mode("unsigned")) comparator_97 (
    .a(ImmSel), .b(3'b010), .eq(comparator_97_eq));  // open: gt, lt
  Comparator #(.width(3), .mode("unsigned")) comparator_98 (
    .a(Instruction_32[14:12]), .b(3'b110), .eq(comparator_98_eq));  // open: gt, lt
  Multiplexer #(.width(4), .enable("false")) multiplexer_22 (
    .in0(multiplexer_21_out), .in1(4'b0100), .out(multiplexer_22_out), .sel(or_9_out));
  or or_9 (or_9_out, and_34_out, and_26_out);
  or or_10 (or_10_out, and_31_out, and_44_out);
  and and_45 (and_45_out, comparator_97_eq, comparator_98_eq);
  Comparator #(.width(3), .mode("unsigned")) comparator_99 (
    .a(ImmSel), .b(3'b010), .eq(comparator_99_eq));  // open: gt, lt
  Comparator #(.width(3), .mode("unsigned")) comparator_100 (
    .a(Instruction_32[14:12]), .b(3'b111), .eq(comparator_100_eq));  // open: gt, lt
  Multiplexer #(.width(4), .enable("false")) multiplexer_23 (
    .in0(multiplexer_22_out), .in1(4'b0011), .out(multiplexer_23_out), .sel(or_10_out));
  or or_11 (or_11_out, and_35_out, and_45_out);
  and and_46 (and_46_out, comparator_99_eq, comparator_100_eq);
  Multiplexer #(.width(4), .enable("false")) multiplexer_24 (
    .in0(multiplexer_23_out), .in1(4'b0010), .out(multiplexer_24_out), .sel(or_11_out));
  Multiplexer #(.width(4), .enable("false")) multiplexer_25 (
    .in0(multiplexer_24_out), .in1(4'b0001), .out(multiplexer_25_out), .sel(or_12_out));
  or or_12 (or_12_out, and_41_out, and_46_out);
  Multiplexer #(.width(4), .enable("false")) multiplexer_26 (
    .in0(multiplexer_25_out), .in1(4'b0000), .out(ALUSel), .sel(or_13_out));
  or or_13 (or_13_out, and_23_out, and_29_out, and_32_out, and_36_out, and_38_out, and_39_out, and_40_out, and_42_out, comparator_93_eq, comparator_94_eq);

  // Other names for the same wires on the sheet: breq_23907428 = BrEq; brlt_24eaaf69 = BrLt; inst_type[2:0] = ImmSel;
  //   instID_I_S_SB[2:0] = Instruction_32[14:12]; instID_R[9:0] = {Instruction_32[31:25], Instruction_32[14:12]};
  //   instID_I_corners[6:0] = Instruction_32[31:25]; instID_U_UJ[6:0] = Instruction_32[6:0]

  // Notes on the sheet:
  //   beq
  //   bne
  //   blt
  //   bltu
  //   Bsel?
  //   Type Determiner
  //   jalr
  //   jal
  //   jalr
  //   lw
  //   lb
  //   lh
  //   R-func7func3
  //   srai, srli, slli-func7
  //   sw
  //   bltu
  //   default_to_ALU
  //   opcode
  //   I/S/SB(B)-func3
  //   default_to_lw
  //   lw
  //   jalr/U/UJ(J)-opcode
  //   PC+4?
  //   lb
  //   lb
  //   beq
  //   bne
  //   blt
  //   bltu
  //   srai, srli, slli-func7
  //   Mem?
  //   lw?
  //   lh
  //   default_to_no branch
  //   ALU?
  //   lb?
  //   lb?
  //   lh
  //   lh?
  //   lh?
  //   bne/bgt?
  //   blt/bltu?
  //   slt
  //   slli
  //   beq?
  //   error_indicator
  //   mulh
  //   srli
  //   add
  //   else-no branching
  //   sub
  //   slti
  //   Mulh?
  //   mulhu
  //   srai
  //   Sub?
  //   mul
  //   lw
  //   Mulhu?
  //   remu
  //   xor
  //   addi
  //   sw
  //   Mul?
  //   divu
  //   srl
  //   or
  //   beq
  //   blt
  //   Remu?
  //   sll
  //   bltu
  //   bne
  //   Divu?
  //   and
  //   jal
  //   jalr
  //   Slt?
  //   xori
  //   Sll?
  //   Sra?
  //   ori
  //   Srl?
  //   andi
  //   Xor?
  //   Or?
  //   And?
  //   Add?
endmodule

module immediate_generator (
  input  [2:0] ImmSel,
  input  [24:0] imm,
  output [31:0] immOut
);

  wire [31:0] i, s, sb, uj;

  assign sb = {{19{imm[24]}}, {imm[24], imm[0], imm[23:18], imm[4:1], 1'b0}};  // Bit_Extender bit_extender_1
  assign i = {{20{imm[24]}}, imm[24:13]};  // Bit_Extender bit_extender_2
  assign s = {{20{imm[24]}}, {imm[24:18], imm[4:0]}};  // Bit_Extender bit_extender_3
  assign uj = {{11{imm[24]}}, {imm[24], imm[12:5], imm[13], imm[23:14], 1'b0}};  // Bit_Extender bit_extender_4
  Multiplexer #(.select(3), .width(32), .enable("false")) multiplexer_1 (
    .in0({32{1'b1}}), .in1({32{1'b1}}), .in2(i), .in3(s), .in4(sb), .in5({imm[24:5], {12{1'b0}}}), .in6(uj),
    .in7({32{1'b1}}), .out(immOut), .sel(ImmSel));

  // Other names for the same wires on the sheet: immIn[24:0] = imm; u[31:12] = imm[24:5]
endmodule

module type_determiner (
  input  [6:0] Opcode,
  output [2:0] InstrType
);

  wire comparator_1_eq, comparator_2_eq, comparator_3_eq, comparator_4_eq, comparator_5_eq, comparator_6_eq,
       comparator_7_eq, comparator_8_eq, or_1_out;
  wire [3:0] adder_1_out, adder_2_out, adder_3_out, adder_4_out, multiplexer_1_out, multiplexer_2_out,
       multiplexer_3_out, multiplexer_4_out, multiplexer_5_out, multiplexer_6_out;
  wire [3:3] adder_5_out;

  Comparator #(.width(7), .mode("unsigned")) comparator_1 (
    .a(Opcode), .b(7'b0110011), .eq(comparator_1_eq));  // open: gt, lt
  Comparator #(.width(7), .mode("unsigned")) comparator_2 (
    .a(Opcode), .b(7'b0000011), .eq(comparator_2_eq));  // open: gt, lt
  Comparator #(.width(7), .mode("unsigned")) comparator_3 (
    .a(Opcode), .b(7'b0010011), .eq(comparator_3_eq));  // open: gt, lt
  Comparator #(.width(7), .mode("unsigned")) comparator_4 (
    .a(Opcode), .b(7'b1100111), .eq(comparator_4_eq));  // open: gt, lt
  Comparator #(.width(7), .mode("unsigned")) comparator_5 (
    .a(Opcode), .b(7'b0100011), .eq(comparator_5_eq));  // open: gt, lt
  Comparator #(.width(7), .mode("unsigned")) comparator_6 (
    .a(Opcode), .b(7'b1100011), .eq(comparator_6_eq));  // open: gt, lt
  Comparator #(.width(7), .mode("unsigned")) comparator_7 (
    .a(Opcode), .b(7'b0110111), .eq(comparator_7_eq));  // open: gt, lt
  Comparator #(.width(7), .mode("unsigned")) comparator_8 (
    .a(Opcode), .b(7'b1101111), .eq(comparator_8_eq));  // open: gt, lt
  Multiplexer #(.width(4), .enable("false")) multiplexer_1 (
    .in0(4'b0000), .in1(4'b0001), .out(multiplexer_1_out), .sel(comparator_1_eq));
  or or_1 (or_1_out, comparator_2_eq, comparator_3_eq, comparator_4_eq);
  Multiplexer #(.width(4), .enable("false")) multiplexer_2 (
    .in0(4'b0000), .in1(4'b0011), .out(multiplexer_2_out), .sel(comparator_5_eq));
  Multiplexer #(.width(4), .enable("false")) multiplexer_3 (
    .in0(4'b0000), .in1(4'b0010), .out(multiplexer_3_out), .sel(or_1_out));
  Multiplexer #(.width(4), .enable("false")) multiplexer_4 (
    .in0(4'b0000), .in1(4'b0100), .out(multiplexer_4_out), .sel(comparator_6_eq));
  Multiplexer #(.width(4), .enable("false")) multiplexer_5 (
    .in0(4'b0000), .in1(4'b0101), .out(multiplexer_5_out), .sel(comparator_7_eq));
  Multiplexer #(.width(4), .enable("false")) multiplexer_6 (
    .in0(4'b0000), .in1(4'b0110), .out(multiplexer_6_out), .sel(comparator_8_eq));
  Adder #(.width(4)) adder_1 (.a(multiplexer_1_out), .b(multiplexer_3_out), .out(adder_1_out));  // open: cin, cout
  Adder #(.width(4)) adder_2 (.a(adder_1_out), .b(multiplexer_2_out), .out(adder_2_out));  // open: cin, cout
  Adder #(.width(4)) adder_3 (.a(adder_2_out), .b(multiplexer_4_out), .out(adder_3_out));  // open: cin, cout
  Adder #(.width(4)) adder_4 (.a(adder_3_out), .b(multiplexer_5_out), .out(adder_4_out));  // open: cin, cout
  Adder #(.width(4)) adder_5 (
    .a(adder_4_out), .b(multiplexer_6_out), .out({adder_5_out[3], InstrType}));  // open: cin, cout

  // Notes on the sheet:
  //   R
  //   I
  //   S
  //   SB
  //   U
  //   UJ
endmodule

module branch_comp (
  input  [31:0] rs1,
  input  [31:0] rs2,
  input  BrUn,
  output BrEq,
  output BrLT
);

  wire comparator_1_eq, comparator_2_eq, comparator_3_lt, comparator_4_lt;

  Comparator #(.width(32)) comparator_1 (.a(rs1), .b(rs2), .eq(comparator_1_eq));  // open: gt, lt
  Comparator #(.width(32), .mode("unsigned")) comparator_2 (.a(rs1), .b(rs2), .eq(comparator_2_eq));  // open: gt, lt
  Comparator #(.width(32)) comparator_3 (.a(rs1), .b(rs2), .lt(comparator_3_lt));  // open: gt, eq
  Comparator #(.width(32), .mode("unsigned")) comparator_4 (.a(rs1), .b(rs2), .lt(comparator_4_lt));  // open: gt, eq
  Multiplexer #(.enable("false")) multiplexer_1 (.in0(comparator_1_eq), .in1(comparator_2_eq), .out(BrEq), .sel(BrUn));
  Multiplexer #(.enable("false")) multiplexer_2 (.in0(comparator_3_lt), .in1(comparator_4_lt), .out(BrLT), .sel(BrUn));

  // Other names for the same wires on the sheet: A[31:0] = rs1; B[31:0] = rs2
endmodule

module lb_lh_splitter (
  input  [31:0] val_at_address,
  input  [24:0] unfiltered_imm,
  input  [31:0] address_to_access,
  output [31:0] lb_val,
  output [31:0] lh_val
);

  wire comparator_1_eq;
  wire [7:0] multiplexer_1_out;
  wire [11:0] divider_1_rem;
  wire [15:0] multiplexer_2_out;
  wire [31:0] divider_2_rem;

  Divider #(.width(12)) divider_1 (.a(unfiltered_imm[24:13]), .b(12'h4), .rem(divider_1_rem));  // open: out, upper
  Divider #(.width(32)) divider_2 (.a(address_to_access), .b(32'h4), .rem(divider_2_rem));  // open: out, upper
  Multiplexer #(.select(2), .width(8), .enable("false")) multiplexer_1 (
    .in0(val_at_address[7:0]), .in1(val_at_address[15:8]), .in2(val_at_address[23:16]),
    .in3(val_at_address[31:24]), .out(multiplexer_1_out), .sel(divider_1_rem[1:0]));
  assign lb_val = {{24{multiplexer_1_out[7]}}, multiplexer_1_out};  // Bit_Extender bit_extender_1
  Comparator #(.width(32), .mode("unsigned")) comparator_1 (
    .a(divider_2_rem), .b(32'h2), .eq(comparator_1_eq));  // open: gt, lt
  Multiplexer #(.width(16), .enable("false")) multiplexer_2 (
    .in0(val_at_address[15:0]), .in1(val_at_address[31:16]), .out(multiplexer_2_out), .sel(comparator_1_eq));
  assign lh_val = {{16{multiplexer_2_out[15]}}, multiplexer_2_out};  // Bit_Extender bit_extender_2

  // Other names for the same wires on the sheet: cor_val[31:0] = val_at_address; immu[24:0] = unfiltered_imm

  // Notes on the sheet:
  //   offset 0
  //   offset 1
  //   offset 2
  //   offset 3
  //   val offset I want
endmodule
