// Logisim project CPU-testing.circ as structural Verilog: 1 circuit, main circuit main
module main (
  output [31:0] ra,
  output [31:0] sp,
  output [31:0] t0,
  output [31:0] t1,
  output [31:0] t2,
  output [31:0] s0,
  output [31:0] s1,
  output [31:0] a0,
  output [31:0] Requested_Address,
  output [31:0] Requested_Instruction,
  output [15:0] Time_Step,
  output halt
);

  wire clk;

  Clock clock_1 (.out(clk));
  // Probe on Requested_Address
  ROM #(.addrWidth(14), .dataWidth(32)) rom_1 (.addr(Requested_Address[15:2]), .data(Requested_Instruction));
  cpu_main main_1 (
    .INSTRUCTION(Requested_Instruction), .CLOCK(clk), .ra(ra), .sp(sp), .t0(t0), .t1(t1), .t2(t2), .s0(s0),
    .s1(s1), .a0(a0), .PROGRAM_COUNTER(Requested_Address));
  // Probe on Requested_Instruction
  Counter #(.width(16), .max('hffff)) counter_1 (.clk(clk), .Q(Time_Step));  // open: clr, load, up, count, D, carry
  Comparator #(.width(16)) comparator_1 (.a(Time_Step), .b(16'h51), .eq(halt));  // open: gt, lt

  // Other names for the same wires on the sheet: fetch_addr[31:0] = Requested_Address;
  //   Instruction[31:0] = Requested_Instruction

  // Notes on the sheet:
  //   contents of rom_1 (hex, n*v repeats v):
  //   00200293 00400313 FFE00393 00100413 02500133 02628133 02728133 40530133 40628133 40730133 00529133
  //   00829133 00029133 00229113 00129113 00029113 0052D133 0082D133 0002D133 0083D133 0022D113 0012D113
  //   0002D113 0013D113 4022D113 4012D113 4002D113 4013D113 0072A133 0053A133 0073A133 FFE2A113 0023A113
  //   FFE3A113 0053F133 0062F133 0052F133 0023F113 0042F113 0022F113 0062E133 0052E133 0053E133 0042E113
  //   0022E113 0023E113 0062C133 0052C133 0053C133 0042C113 0022C113 0023C113 02535133 0253D133 02505133
  //   02537133 0283F133 0253F133 7F800093 4D200293 61800313 0050A023 0060A223 0000A103 0040A103 00008103
  //   00108103 00208103 00308103 00408103 00508103 00009103 00209103 00409103 00007137 00001137 00002137
  //   00100313 01F31313 02633133
  //   YOUR CPU SHOULD FIT IN HERE!
  //   Instruction Memory
  //   Halts Execution After Constant # of Clock Cycles
  //   Constant
endmodule
