// Logisim project alu.circ as structural Verilog: 1 circuit, main circuit alu
module alu (
  input  [31:0] A,
  input  [31:0] B,
  input  [3:0] ALUSel,
  output [31:0] Result
);

  wire comparator_1_lt, multiplexer_1_out, xor_2_out;
  wire [31:0] add0, adder_2_out, adder_4_out, and0, bit_extender_1_out, bit_extender_2_out, divu0, mul0,
       mulh0, mulh1, mulhu0, multiplexer_2_out, multiplexer_3_out, multiplier_1_cout, multiplier_2_out,
       multiplier_3_out, multiplier_6_cout, negator_1_out, negator_2_out, negator_3_out, not_1_out, or0,
       remu0, sll0, slt0, sra0, srl0, sub0, xor0;

  Adder #(.width(32)) adder_1 (.a(A), .b(B), .out(add0));  // open: cin, cout
  assign and0 = A & B;  // AND_Gate and_1, 32 bits wide
  assign or0 = A | B;  // OR_Gate or_1, 32 bits wide
  assign xor0 = A ^ B;  // XOR_Gate xor_1, 32 bits wide
  assign not_1_out = ~B;  // NOT_Gate not_1, 32 bits wide
  Multiplier #(.width(32)) multiplier_1 (.a(A), .b(B), .cout(multiplier_1_cout));  // open: out, cin
  assign bit_extender_1_out = {{31{B[31]}}, B[31]};  // Bit_Extender bit_extender_1
  Adder #(.width(32)) adder_2 (.a(not_1_out), .b(32'h1), .out(adder_2_out));  // open: cin, cout
  Multiplier #(.width(32)) multiplier_2 (.a(A), .b(bit_extender_1_out), .out(multiplier_2_out));  // open: cin, cout
  Adder #(.width(32)) adder_3 (.a(A), .b(adder_2_out), .out(sub0));  // open: cin, cout
  assign bit_extender_2_out = {{31{A[31]}}, A[31]};  // Bit_Extender bit_extender_2
  Adder #(.width(32)) adder_4 (.a(multiplier_2_out), .b(multiplier_1_cout), .out(adder_4_out));  // open: cin, cout
  Multiplier #(.width(32)) multiplier_3 (.a(B), .b(bit_extender_2_out), .out(multiplier_3_out));  // open: cin, cout
  Adder #(.width(32)) adder_5 (.a(multiplier_3_out), .b(adder_4_out), .out(mulh0));  // open: cin, cout
  Shifter #(.width(32), .shift("lr")) shifter_1 (.in(A), .\dist (B[4:0]), .out(srl0));
  Shifter #(.width(32), .shift("ar")) shifter_2 (.in(A), .\dist (B[4:0]), .out(sra0));
  Shifter #(.width(32)) shifter_3 (.in(A), .\dist (B[4:0]), .out(sll0));
  Comparator #(.width(32)) comparator_1 (.a(A), .b(B), .lt(comparator_1_lt));  // open: gt, eq
  Divider #(.width(32)) divider_1 (.a(A), .b(B), .out(divu0));  // open: upper, rem
  Divider #(.width(32)) divider_2 (.a(A), .b(B), .rem(remu0));  // open: out, upper
  Multiplier #(.width(32)) multiplier_4 (.a(A), .b(B), .out(mul0));  // open: cin, cout
  Multiplier #(.width(32)) multiplier_5 (.a(A), .b(B), .cout(mulhu0));  // open: out, cin
  assign slt0 = {{31{1'b0}}, multiplexer_1_out};  // Bit_Extender bit_extender_3
  Multiplexer #(.enable("false")) multiplexer_1 (
    .in0(1'b0), .in1(1'b1), .out(multiplexer_1_out), .sel(comparator_1_lt));
  Negator #(.width(32)) negator_1 (.in(A), .out(negator_1_out));
  Multiplexer #(.width(32), .enable("false")) multiplexer_2 (
    .in0(B), .in1(negator_2_out), .out(multiplexer_2_out), .sel(B[31]));
  Negator #(.width(32)) negator_2 (.in(B), .out(negator_2_out));
  Multiplexer #(.width(32), .enable("false")) multiplexer_3 (
    .in0(A), .in1(negator_1_out), .out(multiplexer_3_out), .sel(A[31]));
  Multiplier #(.width(32)) multiplier_6 (
    .a(multiplexer_3_out), .b(multiplexer_2_out), .cout(multiplier_6_cout));  // open: out, cin
  Negator #(.width(32)) negator_3 (.in(multiplier_6_cout), .out(negator_3_out));
  xor xor_2 (xor_2_out, B[31], A[31]);
  Multiplexer #(.width(32), .enable("false")) multiplexer_4 (
    .in0(multiplier_6_cout), .in1(negator_3_out), .out(mulh1), .sel(xor_2_out));
  Multiplexer #(.select(4), .width(32), .enable("false")) multiplexer_5 (
    .in0(add0), .in1(and0), .in2(or0), .in3(xor0), .in4(srl0), .in5(sra0), .in6(sll0), .in7(slt0),
    .in8(divu0), .in9(remu0), .in10(mul0), .in11(mulhu0), .in12(sub0), .in13(B), .in14(mulh0), .out(Result),
    .sel(ALUSel));  // open: in15

  // Other names for the same wires on the sheet: bsel0[31:0] = B

  // Notes on the sheet:
  //   INPUTS to your circuit
  //   DON'T CHANGE THE LOCATIONS OF THE INPUTS AND OUTPUTS!
  //   OUTPUT from your circuit
endmodule
